# Fritzing sketch flash_motor_shield (saved by Fritzing 0.9.3b)

parts:
  WeMos_D1_Mini_Motor_Shield1 = WeMos D1 Mini Motor Shield
  Part1 = FTDI Basic Programmer

nets:
  N1: WeMos_D1_Mini_Motor_Shield1.3V, WeMos_D1_Mini_Motor_Shield1.RTS
  N2: WeMos_D1_Mini_Motor_Shield1.3V3, Part1.POWER
  N3: WeMos_D1_Mini_Motor_Shield1.D1, Part1.RXI
  N4: WeMos_D1_Mini_Motor_Shield1.D2, Part1.TXO
  N5: WeMos_D1_Mini_Motor_Shield1.G, Part1.GND
