# Fritzing sketch plane (saved by Fritzing 0.9.3b)

parts:
  WeMos_D1_Mini_Motor_Shield1 = WeMos D1 Mini Motor Shield
  WeMos_D1_Mini_Battery_Shield1 = WeMos D1 Mini Battery Shield
  WeMos_D1_Mini1 = WeMos D1 Mini
  M1 = DC Motor
  M2 = DC Motor
  R1 = Resistor [tolerance=±5% resistance=100k package=THT]
  U1 = LIPO-110mAh [package=lipo-110]  # not connected
  J1 = Basic Servo
  J2 = Basic Servo

nets:
  N1: WeMos_D1_Mini_Motor_Shield1.A1, M1.pin_2
  N2: WeMos_D1_Mini_Motor_Shield1.A2, M1.pin_1
  N3: WeMos_D1_Mini_Motor_Shield1.B1, M2.pin_1
  N4: WeMos_D1_Mini_Motor_Shield1.B2, M2.pin_2
  GND1: WeMos_D1_Mini_Motor_Shield1.GND1, J2.gnd
  N5: WeMos_D1_Mini_Motor_Shield1.VM2, R1.Pin_1
  N6: WeMos_D1_Mini_Battery_Shield1.A0, R1.Pin_0
  N7: WeMos_D1_Mini_Battery_Shield1.D0, WeMos_D1_Mini_Battery_Shield1.RST
  N8: WeMos_D1_Mini1.D5, J1.pulse
  N9: WeMos_D1_Mini1.D7, J2.pulse

custom parts:
  WeMos D1 Mini: The D1 mini is a mini wifi board based on ESP-8266EX.
